# Fritzing sketch rough-layout (saved by Fritzing 0.9.5d)
breadboards: 1

parts:
  U2_(22=SCL_21=SDA) = ESP32-38PinWide [part_number=ESP32-38PinWide]
  pH_Circuit1_TX=SDA_RX=SCL = pH Circuit
  OLED1 = OLED 128x64 I2C Monochrome Display GND-VDD

nets (from the schematic view):
  GND: U2_(22=SCL_21=SDA).GND, pH_Circuit1_TX=SDA_RX=SCL.GND#0, OLED1.GND
  VIN: U2_(22=SCL_21=SDA).VIN, pH_Circuit1_TX=SDA_RX=SCL.Vcc, OLED1.VDD
  N1: U2_(22=SCL_21=SDA).GPIO21, pH_Circuit1_TX=SDA_RX=SCL.RX, OLED1.SDA
  N2: U2_(22=SCL_21=SDA).GPIO22, pH_Circuit1_TX=SDA_RX=SCL.TX, OLED1.SCK

notes:
  I2C:
  SDA = 21
  SCK / SCL = 22
  Real PH board is Robo-Tank's
  Takes 5V in

custom parts:
  ESP32-38PinWide: Generic 38-Pin ESP32 with wide format (only access to one side of pins on a breadboard) based on Stephen Lilley's HiLetgo ESP-WROOM-32 ESP32 ESP-32S Development Board.
  OLED 128x64 I2C Monochrome Display GND-VDD: OLED 128x64 I2C Monochrome Display. Note: there are two variants of this part, this one is the GND VDD SCK SDA variant. The other is VDD GND SCK SDA. Make sure you select the part that matches your module as using the incorrect part will probably destroy your module! In addition the mounting holes are marked on silkscreen but not by default drilled. If you want drilled mounting holes, copy a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
